# Fritzing sketch cyd_esp32_pn532_i2c (saved by Fritzing 1.0.6)

parts:
  Composant1 = PN532 Elechouse RFID NFC Module V3
  A1 = ESP32-2432S028R

nets:
  N1: Composant1.GND, A1.Pin_5, A1.Pin_9
  N2: Composant1.VCC, A1.Pin_8
  N3: Composant1.SDA, A1.Pin_7
  N4: Composant1.SCL, A1.Pin_6

custom parts:
  PN532 Elechouse RFID NFC Module V3: NFC is a popular technology in recent years. We often heard this work while smart phone company such as Samsung or HTC introduces their latest high-end phones. Almost all the high-end phone in the market support NFC. Near field communication (NFC) is a set of standards for smart phones and similar devices to establish radio communication with each other by touching them together or bringing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
  ESP32-2432S028R: The ESP32-2432S028R development board.
